// Logisim project 2008007_cs_project.circ as structural Verilog: 12 circuits, main circuit reg_gen
module main (
  input  in_1,
  input  in_2,
  input  in_3,
  input  in_4,
  input  in_5,
  input  in_6,
  input  in_7,
  output [3:0] out_8,
  output [7:0] out_9,
  output [7:0] out_10,
  output [7:0] out_11,
  output [7:0] out_12,
  output [7:0] out_13,
  output [7:0] out_14,
  output [7:0] out_15,
  output [7:0] out_16,
  output [7:0] out_17,
  output [7:0] out_18,
  output [7:0] out_19,
  output [7:0] out_20,
  output [7:0] out_21,
  output [7:0] out_22,
  output [7:0] out_23,
  output [7:0] out_24,
  output [7:0] out_25,
  output [7:0] out_26,
  output [7:0] out_27,
  output [3:0] out_28,
  output [3:0] out_29,
  output [7:0] out_30,
  output [7:0] out_31
);

  wire a_in, a_out, alu_out, alu_sub, b_in, b_out, cs_in, hlt, ins_reg_in_en, ins_reg_out_en, jmp, jump_en,
       mar_in_en, out_in, pc_en, pc_load, pc_out, ram_wr_manual, sram_rd, sram_wr;
  wire [7:0] auto_load_1_sram_ad_out, auto_load_1_sram_ad_out_en, debug_data, multiplexer_1_out;

  Multiplexer #(.width(8)) multiplexer_1 (
    .in0(auto_load_1_sram_ad_out), .in1(out_10), .out(multiplexer_1_out), .sel(cs_in));
  auto_load auto_load_1 (
    .load_en(in_2), .in_2(in_5), .load_clk(in_3), .load_reset(in_6), .debug(in_2), .in_7(in_7),
    .sram_ad_out(auto_load_1_sram_ad_out), .sram_ad_out_en(auto_load_1_sram_ad_out_en), .cs_in(cs_in),
    .sram_wr(ram_wr_manual));  // open: in_5, pc_value
  Hex_Digit_Display hex_digit_display_1 (.value(out_8));  // open: dp
  program_counter program_counter_1 (
    .pc_en(pc_en), .pc_clk(in_3), .pc_reset(in_4), .pc_out_en(pc_out), .pc_load(out_10[3:0]), .jmp(jmp),
    .jump_en(jump_en), .hlt(hlt), .in_9(in_1), .pc_value(out_8), .pc_out(out_10[3:0]));
  sram sram_1 (
    .sram_rd(sram_rd), .sram_wr(sram_wr), .sram_d_in(out_31), .mar_d_in(multiplexer_1_out),
    .mar_in_en(mar_in_en), .s_ram_clk(in_3), .sram_d_out(out_10), .out_8(out_11), .out_9(out_12),
    .out_10(out_13), .out_11(out_14), .out_12(out_15), .out_13(out_16), .out_14(out_17), .out_15(out_18),
    .out_16(out_20), .out_17(out_21), .out_18(out_22), .out_19(out_23), .out_20(out_24), .out_21(out_25),
    .out_22(out_26), .out_23(out_27));
  ROM rom_1 (.addr(auto_load_1_sram_ad_out_en), .data(out_31));
  assign out_10 = in_2 ? debug_data : 8'bz;  // Controlled_Buffer controlled_buffer_1
  Hex_Digit_Display hex_digit_display_2 (.value(out_9[7:4]));  // open: dp
  reg_gen reg_gen_1 (
    .reg_in(out_10), .reg_In_en(a_in), .reg_clk(in_3), .reg_out_en(a_out), .reg_int_out(out_9),
    .reg_out(out_10));
  reg_gen reg_gen_2 (
    .reg_in(out_10), .reg_In_en(b_in), .reg_clk(in_3), .reg_out_en(b_out), .reg_int_out(out_19),
    .reg_out(out_10));
  ins_reg ins_reg_1 (
    .ins_reg_in(out_10), .ins_reg_in_en(ins_reg_in_en), .clock(in_3), .ins_reg_out_en(ins_reg_out_en),
    .add_outs(out_10[3:0]), .ins_out(out_29));
  Hex_Digit_Display hex_digit_display_3 (.value(out_9[3:0]));  // open: dp
  Hex_Digit_Display hex_digit_display_4 (.value(out_19[7:4]));  // open: dp
  Hex_Digit_Display hex_digit_display_5 (.value(out_19[3:0]));  // open: dp
  Hex_Digit_Display hex_digit_display_6 (.value(out_29));  // open: dp
  alu alu_1 (
    .alu_in_1(out_9), .alu_out_en(alu_out), .alu_sub(alu_sub), .alu_in_2(out_19), .alu_out(out_10));  // open: alu_carry_out
  CPU cpu_1 (
    .t_state_en(cs_in), .clk(in_3), .state_reset(in_4), .op_code(out_29), .MAR_in_en_manual(in_2),
    .Debug(in_2), .RAM_wr_manual(ram_wr_manual), .IR_in(ins_reg_in_en), .ram_out(sram_rd),
    .MAR_in(mar_in_en), .ir_out(ins_reg_out_en), .ALU_out(alu_out), .A_in(a_in), .b_in(b_in),
    .RAM_wr(sram_wr), .A_out(a_out), .OUT_in(out_in), .pc_load(pc_load), .ALU_sub(alu_sub), .HLT(hlt),
    .pc_inc(pc_en), .pc_out(pc_out), .jmp(jmp), .jump_en(jump_en));  // open: in_8

  assign out_28 = out_10[3:0];
  assign out_30 = out_10;

  // Other names for the same wires on the sheet: clk = in_3; debug = in_2; load_en = in_2; mar_in_en_manual = in_2;
  //   pc_reset = in_4; sram_d_in[7:0] = out_31

  // Notes on the sheet:
  //   contents of rom_1 (hex, n*v repeats v):
  //   1a 2b 3c 4d 50 70 4*0 a b c d
  //   REG A
  //   REG B
endmodule

module reg_gen (
  input  [7:0] reg_in,
  input  reg_In_en,
  input  reg_clk,
  input  reg_out_en,
  output [7:0] reg_int_out,
  output [7:0] reg_out
);

  wire multiplexer_1_out, multiplexer_2_out, multiplexer_3_out, multiplexer_4_out, multiplexer_5_out,
       multiplexer_6_out, multiplexer_7_out, multiplexer_8_out;

  Multiplexer multiplexer_1 (.in0(reg_int_out[7]), .in1(reg_in[7]), .out(multiplexer_1_out), .sel(reg_In_en));
  Multiplexer multiplexer_2 (.in0(reg_int_out[6]), .in1(reg_in[6]), .out(multiplexer_2_out), .sel(reg_In_en));
  D_Flip_Flop d_ff_1 (.D(multiplexer_1_out), .clk(reg_clk), .Q(reg_int_out[7]));  // open: Qn, preset, reset
  assign reg_out[7] = reg_out_en ? reg_int_out[7] : 1'bz;  // Controlled_Buffer controlled_buffer_1
  Multiplexer multiplexer_3 (.in0(reg_int_out[5]), .in1(reg_in[5]), .out(multiplexer_3_out), .sel(reg_In_en));
  D_Flip_Flop d_ff_2 (.D(multiplexer_2_out), .clk(reg_clk), .Q(reg_int_out[6]));  // open: Qn, preset, reset
  assign reg_out[6] = reg_out_en ? reg_int_out[6] : 1'bz;  // Controlled_Buffer controlled_buffer_2
  Multiplexer multiplexer_4 (.in0(reg_int_out[4]), .in1(reg_in[4]), .out(multiplexer_4_out), .sel(reg_In_en));
  D_Flip_Flop d_ff_3 (.D(multiplexer_3_out), .clk(reg_clk), .Q(reg_int_out[5]));  // open: Qn, preset, reset
  assign reg_out[5] = reg_out_en ? reg_int_out[5] : 1'bz;  // Controlled_Buffer controlled_buffer_3
  Multiplexer multiplexer_5 (.in0(reg_int_out[3]), .in1(reg_in[3]), .out(multiplexer_5_out), .sel(reg_In_en));
  D_Flip_Flop d_ff_4 (.D(multiplexer_4_out), .clk(reg_clk), .Q(reg_int_out[4]));  // open: Qn, preset, reset
  assign reg_out[4] = reg_out_en ? reg_int_out[4] : 1'bz;  // Controlled_Buffer controlled_buffer_4
  Multiplexer multiplexer_6 (.in0(reg_int_out[2]), .in1(reg_in[2]), .out(multiplexer_6_out), .sel(reg_In_en));
  D_Flip_Flop d_ff_5 (.D(multiplexer_5_out), .clk(reg_clk), .Q(reg_int_out[3]));  // open: Qn, preset, reset
  assign reg_out[3] = reg_out_en ? reg_int_out[3] : 1'bz;  // Controlled_Buffer controlled_buffer_5
  Multiplexer multiplexer_7 (.in0(reg_int_out[1]), .in1(reg_in[1]), .out(multiplexer_7_out), .sel(reg_In_en));
  D_Flip_Flop d_ff_6 (.D(multiplexer_6_out), .clk(reg_clk), .Q(reg_int_out[2]));  // open: Qn, preset, reset
  assign reg_out[2] = reg_out_en ? reg_int_out[2] : 1'bz;  // Controlled_Buffer controlled_buffer_6
  Multiplexer multiplexer_8 (.in0(reg_int_out[0]), .in1(reg_in[0]), .out(multiplexer_8_out), .sel(reg_In_en));
  D_Flip_Flop d_ff_7 (.D(multiplexer_7_out), .clk(reg_clk), .Q(reg_int_out[1]));  // open: Qn, preset, reset
  assign reg_out[1] = reg_out_en ? reg_int_out[1] : 1'bz;  // Controlled_Buffer controlled_buffer_7
  D_Flip_Flop d_ff_8 (.D(multiplexer_8_out), .clk(reg_clk), .Q(reg_int_out[0]));  // open: Qn, preset, reset
  assign reg_out[0] = reg_out_en ? reg_int_out[0] : 1'bz;  // Controlled_Buffer controlled_buffer_8

  // Notes on the sheet:
  //   input
  //   input Control
  //   Clock
  //   Output Control
  //   Memory
  //   Output
  //   Internal Output
endmodule

module alu (
  input  [7:0] alu_in_1,
  input  alu_out_en,
  input  alu_sub,
  input  [7:0] alu_in_2,
  output [7:0] alu_out,
  output alu_carry_out
);

  wire adder_2_cout, adder_3_cout, adder_4_cout, adder_5_cout, adder_6_cout, adder_7_cout, adder_8_cout,
       xor_1_out, xor_2_out, xor_3_out, xor_4_out, xor_5_out, xor_6_out, xor_7_out, xor_8_out;
  wire [7:0] adder_8_out;

  xor xor_1 (xor_1_out, alu_in_2[7], alu_sub);
  Adder #(.width(1)) adder_1 (
    .a(alu_in_1[7]), .b(xor_1_out), .out(adder_8_out[7]), .cin(adder_2_cout), .cout(alu_carry_out));
  xor xor_2 (xor_2_out, alu_in_2[6], alu_sub);
  Adder #(.width(1)) adder_2 (
    .a(alu_in_1[6]), .b(xor_2_out), .out(adder_8_out[6]), .cin(adder_3_cout), .cout(adder_2_cout));
  xor xor_3 (xor_3_out, alu_in_2[5], alu_sub);
  Adder #(.width(1)) adder_3 (
    .a(alu_in_1[5]), .b(xor_3_out), .out(adder_8_out[5]), .cin(adder_4_cout), .cout(adder_3_cout));
  xor xor_4 (xor_4_out, alu_in_2[4], alu_sub);
  Adder #(.width(1)) adder_4 (
    .a(alu_in_1[4]), .b(xor_4_out), .out(adder_8_out[4]), .cin(adder_5_cout), .cout(adder_4_cout));
  xor xor_5 (xor_5_out, alu_in_2[3], alu_sub);
  Adder #(.width(1)) adder_5 (
    .a(alu_in_1[3]), .b(xor_5_out), .out(adder_8_out[3]), .cin(adder_6_cout), .cout(adder_5_cout));
  xor xor_6 (xor_6_out, alu_in_2[2], alu_sub);
  Adder #(.width(1)) adder_6 (
    .a(alu_in_1[2]), .b(xor_6_out), .out(adder_8_out[2]), .cin(adder_7_cout), .cout(adder_6_cout));
  xor xor_7 (xor_7_out, alu_in_2[1], alu_sub);
  Adder #(.width(1)) adder_7 (
    .a(alu_in_1[1]), .b(xor_7_out), .out(adder_8_out[1]), .cin(adder_8_cout), .cout(adder_7_cout));
  xor xor_8 (xor_8_out, alu_in_2[0], alu_sub);
  Adder #(.width(1)) adder_8 (.a(alu_in_1[0]), .b(xor_8_out), .out(adder_8_out[0]), .cin(alu_sub), .cout(adder_8_cout));
  assign alu_out = alu_out_en ? adder_8_out : 8'bz;  // Controlled_Buffer controlled_buffer_1

  // Notes on the sheet:
  //   Carry Output
  //   Subtract Control
  //   Input 1
  //   Full Adders
  //   Output
  //   Output Control
  //   Alu Output
endmodule

module program_counter (
  input  pc_en,
  input  pc_clk,
  input  pc_reset,
  input  pc_out_en,
  input  [3:0] pc_load,
  input  jmp,
  input  jump_en,
  input  hlt,
  input  in_9,
  output [3:0] pc_value,
  output [3:0] pc_out
);

  wire j_k_ff_2_qn, j_k_ff_3_qn, j_k_ff_4_qn, multiplexer_1_out, multiplexer_3_out, multiplexer_5_out;
  wire [3:0] d_ff_4_q, multiplexer_2_out, multiplexer_4_out;

  J_K_Flip_Flop j_k_ff_1 (
    .J(multiplexer_3_out), .K(multiplexer_3_out), .clk(j_k_ff_2_qn), .Q(pc_value[3]),
    .reset(multiplexer_1_out));  // open: Qn, preset
  Multiplexer multiplexer_1 (.in0(pc_reset), .in1(in_9), .out(multiplexer_1_out), .sel(hlt));
  J_K_Flip_Flop j_k_ff_2 (
    .J(multiplexer_3_out), .K(multiplexer_3_out), .clk(j_k_ff_3_qn), .Q(pc_value[2]), .Qn(j_k_ff_2_qn),
    .reset(multiplexer_1_out));  // open: preset
  Multiplexer #(.width(4)) multiplexer_2 (.in1(pc_load), .out(multiplexer_2_out), .sel(jump_en));  // open: in0
  J_K_Flip_Flop j_k_ff_3 (
    .J(multiplexer_3_out), .K(multiplexer_3_out), .clk(j_k_ff_4_qn), .Q(pc_value[1]), .Qn(j_k_ff_3_qn),
    .reset(multiplexer_1_out));  // open: preset
  D_Flip_Flop d_ff_1 (.D(multiplexer_2_out[3]), .clk(pc_clk), .Q(d_ff_4_q[3]));  // open: Qn, preset, reset
  J_K_Flip_Flop j_k_ff_4 (
    .J(multiplexer_3_out), .K(multiplexer_3_out), .clk(pc_clk), .Q(pc_value[0]), .Qn(j_k_ff_4_qn),
    .reset(multiplexer_1_out));  // open: preset
  D_Flip_Flop d_ff_2 (.D(multiplexer_2_out[2]), .clk(pc_clk), .Q(d_ff_4_q[2]));  // open: Qn, preset, reset
  Multiplexer multiplexer_3 (.in0(pc_en), .in1(in_9), .out(multiplexer_3_out), .sel(hlt));
  D_Flip_Flop d_ff_3 (.D(multiplexer_2_out[1]), .clk(pc_clk), .Q(d_ff_4_q[1]));  // open: Qn, preset, reset
  D_Flip_Flop d_ff_4 (.D(multiplexer_2_out[0]), .clk(pc_clk), .Q(d_ff_4_q[0]));  // open: Qn, preset, reset
  Multiplexer #(.width(4)) multiplexer_4 (.in0(pc_value), .in1(d_ff_4_q), .out(multiplexer_4_out), .sel(jmp));
  assign pc_out = multiplexer_5_out ? multiplexer_4_out : 4'bz;  // Controlled_Buffer controlled_buffer_1
  Multiplexer multiplexer_5 (.in0(pc_out_en), .in1(in_9), .out(multiplexer_5_out), .sel(hlt));

  // Notes on the sheet:
  //   Clock
  //   Reset
  //   Count Control
  //   Output Control
  //   Counter Output
endmodule

module dec (
  input  [3:0] dec_sel,
  output [15:0] dec_out
);

  wire not_1_out, not_2_out, not_3_out, not_4_out;

  not not_1 (not_1_out, dec_sel[3]);
  not not_2 (not_2_out, dec_sel[2]);
  not not_3 (not_3_out, dec_sel[1]);
  not not_4 (not_4_out, dec_sel[0]);
  and and_1 (dec_out[0], not_4_out, not_3_out, not_2_out, not_1_out);
  and and_2 (dec_out[1], dec_sel[0], not_3_out, not_2_out, not_1_out);
  and and_3 (dec_out[2], not_4_out, dec_sel[1], not_2_out, not_1_out);
  and and_4 (dec_out[3], dec_sel[0], dec_sel[1], not_2_out, not_1_out);
  and and_5 (dec_out[4], not_4_out, not_3_out, dec_sel[2], not_1_out);
  and and_6 (dec_out[5], dec_sel[0], not_3_out, dec_sel[2], not_1_out);
  and and_7 (dec_out[6], not_4_out, dec_sel[1], dec_sel[2], not_1_out);
  and and_8 (dec_out[7], dec_sel[0], dec_sel[1], dec_sel[2], not_1_out);
  and and_9 (dec_out[8], not_4_out, not_3_out, not_2_out, dec_sel[3]);
  and and_10 (dec_out[9], dec_sel[0], not_3_out, not_2_out, dec_sel[3]);
  and and_11 (dec_out[10], not_4_out, dec_sel[1], not_2_out, dec_sel[3]);
  and and_12 (dec_out[11], dec_sel[0], dec_sel[1], not_2_out, dec_sel[3]);
  and and_13 (dec_out[12], not_4_out, not_3_out, dec_sel[2], dec_sel[3]);
  and and_14 (dec_out[13], dec_sel[0], not_3_out, dec_sel[2], dec_sel[3]);
  and and_15 (dec_out[14], not_4_out, dec_sel[1], dec_sel[2], dec_sel[3]);
  and and_16 (dec_out[15], dec_sel[0], dec_sel[1], dec_sel[2], dec_sel[3]);
endmodule

module s_ram_cell (
  input  [7:0] data_in,
  input  wr_en,
  input  clk,
  input  cs,
  input  rd_en,
  output [7:0] memory_content,
  output [7:0] data_out
);

  wire and_1_out, and_2_out;

  and and_1 (and_1_out, wr_en, cs);
  and and_2 (and_2_out, cs, rd_en);
  reg_gen reg_gen_1 (
    .reg_in(data_in), .reg_In_en(and_1_out), .reg_clk(clk), .reg_out_en(and_2_out),
    .reg_int_out(memory_content), .reg_out(data_out));
endmodule

module sram (
  input  sram_rd,
  input  sram_wr,
  input  [7:0] sram_d_in,
  input  [7:0] mar_d_in,
  input  mar_in_en,
  input  s_ram_clk,
  output [7:0] sram_d_out,
  output [7:0] out_8,
  output [7:0] out_9,
  output [7:0] out_10,
  output [7:0] out_11,
  output [7:0] out_12,
  output [7:0] out_13,
  output [7:0] out_14,
  output [7:0] out_15,
  output [7:0] out_16,
  output [7:0] out_17,
  output [7:0] out_18,
  output [7:0] out_19,
  output [7:0] out_20,
  output [7:0] out_21,
  output [7:0] out_22,
  output [7:0] out_23
);

  wire [7:0] controlled_buffer_1_out, reg_gen_1_reg_int_out;
  wire [15:0] dec_1_dec_out;

  reg_gen reg_gen_1 (
    .reg_in(mar_d_in), .reg_In_en(mar_in_en), .reg_clk(s_ram_clk), .reg_int_out(reg_gen_1_reg_int_out));  // open: reg_out_en, reg_out
  dec dec_1 (.dec_sel(reg_gen_1_reg_int_out[3:0]), .dec_out(dec_1_dec_out));
  assign controlled_buffer_1_out = sram_wr ? sram_d_in : 8'bz;  // Controlled_Buffer controlled_buffer_1
  s_ram_cell s_ram_cell_1 (
    .data_in(controlled_buffer_1_out), .wr_en(sram_wr), .clk(s_ram_clk), .cs(dec_1_dec_out[0]),
    .rd_en(sram_rd), .memory_content(out_8), .data_out(controlled_buffer_1_out));
  s_ram_cell s_ram_cell_2 (
    .data_in(controlled_buffer_1_out), .wr_en(sram_wr), .clk(s_ram_clk), .cs(dec_1_dec_out[1]),
    .rd_en(sram_rd), .memory_content(out_9), .data_out(controlled_buffer_1_out));
  s_ram_cell s_ram_cell_3 (
    .data_in(controlled_buffer_1_out), .wr_en(sram_wr), .clk(s_ram_clk), .cs(dec_1_dec_out[2]),
    .rd_en(sram_rd), .memory_content(out_10), .data_out(controlled_buffer_1_out));
  s_ram_cell s_ram_cell_4 (
    .data_in(controlled_buffer_1_out), .wr_en(sram_wr), .clk(s_ram_clk), .cs(dec_1_dec_out[3]),
    .rd_en(sram_rd), .memory_content(out_11), .data_out(controlled_buffer_1_out));
  s_ram_cell s_ram_cell_5 (
    .data_in(controlled_buffer_1_out), .wr_en(sram_wr), .clk(s_ram_clk), .cs(dec_1_dec_out[4]),
    .rd_en(sram_rd), .memory_content(out_12), .data_out(controlled_buffer_1_out));
  s_ram_cell s_ram_cell_6 (
    .data_in(controlled_buffer_1_out), .wr_en(sram_wr), .clk(s_ram_clk), .cs(dec_1_dec_out[5]),
    .rd_en(sram_rd), .memory_content(out_13), .data_out(controlled_buffer_1_out));
  s_ram_cell s_ram_cell_7 (
    .data_in(controlled_buffer_1_out), .wr_en(sram_wr), .clk(s_ram_clk), .cs(dec_1_dec_out[6]),
    .rd_en(sram_rd), .memory_content(out_14), .data_out(controlled_buffer_1_out));
  s_ram_cell s_ram_cell_8 (
    .data_in(controlled_buffer_1_out), .wr_en(sram_wr), .clk(s_ram_clk), .cs(dec_1_dec_out[7]),
    .rd_en(sram_rd), .memory_content(out_15), .data_out(controlled_buffer_1_out));
  s_ram_cell s_ram_cell_9 (
    .data_in(controlled_buffer_1_out), .wr_en(sram_wr), .clk(s_ram_clk), .cs(dec_1_dec_out[8]),
    .rd_en(sram_rd), .memory_content(out_16), .data_out(controlled_buffer_1_out));
  s_ram_cell s_ram_cell_10 (
    .data_in(controlled_buffer_1_out), .wr_en(sram_wr), .clk(s_ram_clk), .cs(dec_1_dec_out[9]),
    .rd_en(sram_rd), .memory_content(out_17), .data_out(controlled_buffer_1_out));
  s_ram_cell s_ram_cell_11 (
    .data_in(controlled_buffer_1_out), .wr_en(sram_wr), .clk(s_ram_clk), .cs(dec_1_dec_out[10]),
    .rd_en(sram_rd), .memory_content(out_18), .data_out(controlled_buffer_1_out));
  s_ram_cell s_ram_cell_12 (
    .data_in(controlled_buffer_1_out), .wr_en(sram_wr), .clk(s_ram_clk), .cs(dec_1_dec_out[11]),
    .rd_en(sram_rd), .memory_content(out_19), .data_out(controlled_buffer_1_out));
  s_ram_cell s_ram_cell_13 (
    .data_in(controlled_buffer_1_out), .wr_en(sram_wr), .clk(s_ram_clk), .cs(dec_1_dec_out[12]),
    .rd_en(sram_rd), .memory_content(out_20), .data_out(controlled_buffer_1_out));
  s_ram_cell s_ram_cell_14 (
    .data_in(controlled_buffer_1_out), .wr_en(sram_wr), .clk(s_ram_clk), .cs(dec_1_dec_out[13]),
    .rd_en(sram_rd), .memory_content(out_21), .data_out(controlled_buffer_1_out));
  s_ram_cell s_ram_cell_15 (
    .data_in(controlled_buffer_1_out), .wr_en(sram_wr), .clk(s_ram_clk), .cs(dec_1_dec_out[14]),
    .rd_en(sram_rd), .memory_content(out_22), .data_out(controlled_buffer_1_out));
  s_ram_cell s_ram_cell_16 (
    .data_in(controlled_buffer_1_out), .wr_en(sram_wr), .clk(s_ram_clk), .cs(dec_1_dec_out[15]),
    .rd_en(sram_rd), .memory_content(out_23), .data_out(controlled_buffer_1_out));
  assign sram_d_out = sram_rd ? controlled_buffer_1_out : 8'bz;  // Controlled_Buffer controlled_buffer_2
endmodule

module ins_reg (
  input  [7:0] ins_reg_in,
  input  ins_reg_in_en,
  input  clock,
  input  ins_reg_out_en,
  output [3:0] add_outs,
  output [3:0] ins_out
);

  wire [3:0] reg_gen_1_reg_int_out;

  reg_gen reg_gen_1 (
    .reg_in(ins_reg_in), .reg_In_en(ins_reg_in_en), .reg_clk(clock),
    .reg_int_out({ins_out, reg_gen_1_reg_int_out}));  // open: reg_out_en, reg_out
  assign add_outs = ins_reg_out_en ? reg_gen_1_reg_int_out : 4'bz;  // Controlled_Buffer controlled_buffer_1
endmodule

module opcode_dec (
  input  [3:0] ir_MSB,
  output isLDA,
  output isADD,
  output isSUB,
  output isSTA,
  output isJMP,
  output isOUT,
  output isHLT
);

  wire [15:0] dec_1_dec_out;

  dec dec_1 (
    .dec_sel(ir_MSB),
    .dec_out({dec_1_dec_out[15:8], isHLT, isOUT, isJMP, isSTA, isSUB, isADD, isLDA, dec_1_dec_out[0]}));
endmodule

module state_counter (
  input  rc_en,
  input  clk,
  input  ring_reset,
  output T1,
  output T2,
  output T3,
  output T4,
  output T5,
  output T6
);

  wire controlled_buffer_1_out, not_1_out;
  wire [3:0] program_counter_1_pc_value;
  wire [15:0] dec_1_dec_out;

  assign controlled_buffer_1_out = ring_reset ? ring_reset : 1'bz;  // Controlled_Buffer controlled_buffer_1
  assign controlled_buffer_1_out = not_1_out ? dec_1_dec_out[7] : 1'bz;  // Controlled_Buffer controlled_buffer_2
  not not_1 (not_1_out, ring_reset);
  program_counter program_counter_1 (
    .pc_en(rc_en), .pc_clk(clk), .pc_reset(controlled_buffer_1_out), .pc_out_en(rc_en),
    .pc_value(program_counter_1_pc_value));  // open: pc_load, jmp, jump_en, hlt, in_9, pc_out
  dec dec_1 (
    .dec_sel(program_counter_1_pc_value),
    .dec_out({dec_1_dec_out[15:7], T6, T5, T4, T3, T2, T1, dec_1_dec_out[0]}));
endmodule

module CPU (
  input  t_state_en,
  input  clk,
  input  state_reset,
  input  [3:0] op_code,
  input  MAR_in_en_manual,
  input  Debug,
  input  RAM_wr_manual,
  input  in_8,
  output IR_in,
  output ram_out,
  output MAR_in,
  output ir_out,
  output ALU_out,
  output A_in,
  output b_in,
  output RAM_wr,
  output A_out,
  output OUT_in,
  output pc_load,
  output ALU_sub,
  output HLT,
  output pc_inc,
  output pc_out,
  output jmp,
  output jump_en
);

  wire and_2_out, and_3_out, and_4_out, and_6_out, and_7_out, and_9_out, and_10_out, multiplexer_1_out,
       multiplexer_3_out, not_1_out, not_2_out, opcode_dec_1_isadd, opcode_dec_1_ishlt, opcode_dec_1_isjmp,
       opcode_dec_1_islda, opcode_dec_1_isout, opcode_dec_1_issta, opcode_dec_1_issub, or_2_out, or_3_out,
       or_4_out, or_5_out, or_6_out, or_10_out, state_counter_1_t1, state_counter_1_t3, state_counter_1_t4,
       state_counter_1_t5, state_counter_1_t6;

  Multiplexer multiplexer_1 (.in0(t_state_en), .in1(in_8), .out(multiplexer_1_out), .sel(opcode_dec_1_ishlt));
  state_counter state_counter_1 (
    .rc_en(multiplexer_1_out), .clk(clk), .ring_reset(state_reset), .T1(state_counter_1_t1), .T2(IR_in),
    .T3(state_counter_1_t3), .T4(state_counter_1_t4), .T5(state_counter_1_t5), .T6(state_counter_1_t6));
  opcode_dec opcode_dec_1 (
    .ir_MSB(op_code), .isLDA(opcode_dec_1_islda), .isADD(opcode_dec_1_isadd), .isSUB(opcode_dec_1_issub),
    .isSTA(opcode_dec_1_issta), .isJMP(opcode_dec_1_isjmp), .isOUT(opcode_dec_1_isout),
    .isHLT(opcode_dec_1_ishlt));
  not not_1 (not_1_out, opcode_dec_1_ishlt);
  and and_1 (pc_inc, state_counter_1_t3, and_2_out);
  not not_2 (not_2_out, opcode_dec_1_isjmp);
  and and_2 (and_2_out, not_1_out, not_2_out);
  or or_1 (pc_out, state_counter_1_t1, jump_en);
  or or_2 (or_2_out, opcode_dec_1_islda, opcode_dec_1_isadd, opcode_dec_1_issub, opcode_dec_1_issta, opcode_dec_1_isjmp);
  or or_3 (or_3_out, opcode_dec_1_isjmp, opcode_dec_1_issta, opcode_dec_1_issub, opcode_dec_1_isadd, opcode_dec_1_islda);
  or or_4 (or_4_out, opcode_dec_1_isadd, opcode_dec_1_issub);
  or or_5 (or_5_out, opcode_dec_1_islda, opcode_dec_1_isadd, opcode_dec_1_issub);
  and and_3 (and_3_out, state_counter_1_t4, or_2_out);
  and and_4 (and_4_out, state_counter_1_t5, or_5_out);
  and and_5 (ir_out, state_counter_1_t4, or_3_out);
  and and_6 (and_6_out, opcode_dec_1_islda, state_counter_1_t5);
  and and_7 (and_7_out, state_counter_1_t6, or_4_out);
  and and_8 (b_in, opcode_dec_1_isadd, state_counter_1_t5);
  and and_9 (and_9_out, state_counter_1_t4, opcode_dec_1_isout);
  and and_10 (and_10_out, state_counter_1_t5, opcode_dec_1_issta);
  and and_11 (pc_load, state_counter_1_t4, opcode_dec_1_isjmp);
  and and_12 (ALU_sub, state_counter_1_t6, opcode_dec_1_issub);
  and and_13 (HLT, state_counter_1_t4, opcode_dec_1_ishlt);
  or or_6 (or_6_out, state_counter_1_t1, and_3_out);
  and and_14 (ALU_out, state_counter_1_t6, or_4_out);
  or or_7 (A_in, and_6_out, and_7_out);
  or or_8 (A_out, and_9_out, and_10_out);
  and and_15 (OUT_in, state_counter_1_t4, opcode_dec_1_isout);
  or or_9 (ram_out, IR_in, and_4_out);
  or or_10 (or_10_out, state_counter_1_t1, state_counter_1_t4);
  Multiplexer multiplexer_2 (.in0(or_6_out), .in1(MAR_in_en_manual), .out(MAR_in), .sel(Debug));
  Multiplexer multiplexer_3 (.in0(and_9_out), .in1(RAM_wr_manual), .out(multiplexer_3_out), .sel(Debug));
  and and_16 (jump_en, opcode_dec_1_isjmp, state_counter_1_t4);
  and and_17 (jmp, or_10_out, opcode_dec_1_isjmp);
  or or_11 (RAM_wr, multiplexer_3_out, A_out);

  // Notes on the sheet:
  //   ddd
  //   ddd
  //   ddd
  //   ddd
  //   ddd
  //   ddd
  //   ddd
  //   ddd
  //   ddd
  //   ddd
  //   ddd
endmodule

module auto_load (
  input  load_en,
  input  in_2,
  input  load_clk,
  input  load_reset,
  input  [3:0] in_5,
  input  debug,
  input  in_7,
  output [3:0] pc_value,
  output [7:0] sram_ad_out,
  output [7:0] sram_ad_out_en,
  output cs_in,
  output sram_wr
);

  wire j_k_ff_2_qn, j_k_ff_3_qn, j_k_ff_4_qn, multiplexer_1_out, multiplexer_2_out, not_1_out;

  J_K_Flip_Flop j_k_ff_1 (
    .J(multiplexer_2_out), .K(multiplexer_2_out), .clk(j_k_ff_2_qn), .Q(pc_value[3]), .reset(load_reset));  // open: Qn, preset
  not not_1 (not_1_out, load_clk);
  Multiplexer multiplexer_1 (.in0(debug), .in1(in_7), .out(multiplexer_1_out), .sel(cs_in));
  and and_1 (sram_wr, not_1_out, multiplexer_1_out);
  J_K_Flip_Flop j_k_ff_2 (
    .J(multiplexer_2_out), .K(multiplexer_2_out), .clk(j_k_ff_3_qn), .Q(pc_value[2]), .Qn(j_k_ff_2_qn),
    .reset(load_reset));  // open: preset
  J_K_Flip_Flop j_k_ff_3 (
    .J(multiplexer_2_out), .K(multiplexer_2_out), .clk(j_k_ff_4_qn), .Q(pc_value[1]), .Qn(j_k_ff_3_qn),
    .reset(load_reset));  // open: preset
  J_K_Flip_Flop j_k_ff_4 (
    .J(multiplexer_2_out), .K(multiplexer_2_out), .clk(load_clk), .Q(pc_value[0]), .Qn(j_k_ff_4_qn),
    .reset(load_reset));  // open: preset
  Multiplexer multiplexer_2 (.in0(load_en), .in1(in_2), .out(multiplexer_2_out), .sel(cs_in));
  Register register_1 (.D({in_5, pc_value}), .en(load_clk), .clk(load_clk), .Q(sram_ad_out_en));  // open: clr
  and and_2 (cs_in, pc_value[3], pc_value[2], pc_value[1], pc_value[0]);

  assign sram_ad_out = {in_5, pc_value};

  // Notes on the sheet:
  //   Clock
  //   Count Control
  //   Counter Output
endmodule
